# Fritzing sketch Screens_V2 (saved by Fritzing 0.9.3b)

parts:
  S1 = H-Bridge with L298N
  End_switch_up = KY-003 Hall Magnetic Sensor Module [package="Breakout board"]
  End_switch_down = KY-003 Hall Magnetic Sensor Module [package="Breakout board"]
  Up = Round Pushbutton
  Down = Round Pushbutton
  WeMos_D1_Mini1 = WeMos D1 Mini
  M1 = DC Motor

nets:
  N1: S1.GND, End_switch_up.-, End_switch_down.-, Up.leg1, Down.leg1, WeMos_D1_Mini1.G
  5V: S1.5V, End_switch_up.Vin, End_switch_down.Vin, WeMos_D1_Mini1.5V
  N2: S1.IN3, WeMos_D1_Mini1.D1
  N3: S1.IN4, WeMos_D1_Mini1.D2
  N4: S1.M2-01, M1.pin_2
  N5: S1.M2-02, M1.pin_1
  N6: End_switch_up.S, WeMos_D1_Mini1.D3
  N7: End_switch_down.S, WeMos_D1_Mini1.D4
  N8: Up.leg0, WeMos_D1_Mini1.D6
  N9: Down.leg0, WeMos_D1_Mini1.D7

notes:
  Sunscreen / curtain controller
  12v power

custom parts:
  H-Bridge with L298N: h-bridge
  KY-003 Hall Magnetic Sensor Module: KEYES KY-003 Arduino Hall Magnetic Sensor Module is a switch that will turn on/off in the presence of a magnetic field.
