# Fritzing sketch Screens_V2_relais (saved by Fritzing 0.9.3b)

parts:
  Up = Round Pushbutton
  Down = Round Pushbutton
  WeMos_D1_Mini1 = WeMos D1 Mini
  U1 = 2-Channel 5v Relay Shield [package=relay-2ch5v10a]

nets:
  N1: Up.leg0, WeMos_D1_Mini1.D6
  N2: Down.leg0, WeMos_D1_Mini1.D7
  5V: WeMos_D1_Mini1.5V, U1.VCC
  N3: WeMos_D1_Mini1.D1, U1.IN1
  N4: WeMos_D1_Mini1.D2, U1.IN2
  N5: WeMos_D1_Mini1.G, U1.GND

notes:
  Sunscreen / curtain controller
  5v power
  230volt
  buismotor
  use relais shield with optoco

custom parts:
  2-Channel 5v Relay Shield: 2 Channel 5v Relay Shield w. 2x SPD-06VDC-SD-C
